// Logisim project CPU_MIPS.circ as structural Verilog: 5 circuits, main circuit main
module main (
  input  in_1
);

  wire clock, depende_1_r, mostrar_1_add, mostrar_1_branch, mostrar_1_jump, mostrar_1_load, mostrar_1_r,
       mostrar_1_store, Reset, selec;
  wire [4:0] multiplexer_1_out, separadores_1_rd, separadores_1_rs, separadores_1_rt, separadores_1_shamt;
  wire [5:0] separadores_1_funct, separadores_1_opcode;
  wire [15:0] separadores_1_offset;
  wire [23:0] bit_extender_1_out;
  wire [25:0] separadores_1_jump;
  wire [31:0] adder_1_out, adder_2_out, bit_extender_2_out, multiplexer_2_out, ram_1_data, register_1_q,
       unidad_de_registros_1_dato_1, unidad_de_registros_1_dato_2;

  Clock clock_1 (.out(clock));
  Button button_1 (.out(Reset));
  Register #(.width(32)) register_1 (.D(adder_1_out), .en(1'b1), .Q(register_1_q), .clk(clock), .clr(Reset));
  Adder #(.width(32)) adder_1 (.a(32'h1), .b(register_1_q), .out(adder_1_out));  // open: cin, cout
  Bit_Extender #(.in_width(32), .out_width(24)) bit_extender_1 (.in(register_1_q), .out(bit_extender_1_out));
  RAM #(.addrWidth(24), .dataWidth(32)) ram_1 (
    .addr(bit_extender_1_out), .data(ram_1_data));  // open: sel, clk, ld, clr
  // Probe on separadores_1_jump
  // Probe on separadores_1_rd
  // Probe on separadores_1_rt
  // Probe on separadores_1_rs
  // Probe on separadores_1_opcode
  Separadores separadores_1 (
    .in_1(ram_1_data), .Funct(separadores_1_funct), .Shamt(separadores_1_shamt), .RD(separadores_1_rd),
    .RT(separadores_1_rt), .RS(separadores_1_rs), .Opcode(separadores_1_opcode),
    .Offset(separadores_1_offset), .Jump(separadores_1_jump));
  // Probe on separadores_1_offset
  // Probe on separadores_1_shamt
  // Probe on separadores_1_funct
  depende depende_1 (.in_1(separadores_1_opcode), .r(depende_1_r));  // open: add
  mostrar mostrar_1 (
    .in_1(separadores_1_opcode), .r(mostrar_1_r), .add(mostrar_1_add), .load(mostrar_1_load),
    .store(mostrar_1_store), .branch(mostrar_1_branch), .Jump(mostrar_1_jump));
  Multiplexer #(.width(5)) multiplexer_1 (
    .in0(separadores_1_rt), .in1(separadores_1_rd), .out(multiplexer_1_out), .sel(selec));  // open: en
  assign bit_extender_2_out = {{16{1'b0}}, separadores_1_offset};  // Bit_Extender bit_extender_2
  LED led_1 (.in(in_1));
  not not_1 (selec, depende_1_r);
  LED r (.in(mostrar_1_r));
  LED add (.in(mostrar_1_add));
  LED load (.in(mostrar_1_load));
  LED store (.in(mostrar_1_store));
  LED branch (.in(mostrar_1_branch));
  LED jump_2 (.in(mostrar_1_jump));
  Unidad_de_Registros unidad_de_registros_1 (
    .reset(Reset), .clk(clock), .rs(separadores_1_rs), .rt(separadores_1_rt), .rw(multiplexer_1_out),
    .Result(adder_2_out), .dato_1(unidad_de_registros_1_dato_1), .dato_2(unidad_de_registros_1_dato_2));
  // Probe on unidad_de_registros_1_dato_1
  Multiplexer #(.width(32)) multiplexer_2 (
    .in0(unidad_de_registros_1_dato_2), .in1(bit_extender_2_out), .out(multiplexer_2_out), .sel(selec));  // open: en
  Adder #(.width(32)) adder_2 (
    .a(unidad_de_registros_1_dato_1), .b(multiplexer_2_out), .out(adder_2_out));  // open: cin, cout
  // Probe on multiplexer_2_out
  // Probe on adder_2_out
endmodule

module Separadores (
  input  [31:0] in_1,
  output [5:0] Funct,
  output [4:0] Shamt,
  output [4:0] RD,
  output [4:0] RT,
  output [4:0] RS,
  output [5:0] Opcode,
  output [15:0] Offset,
  output [25:0] Jump
);


  assign Funct = in_1[5:0];
  assign Jump = in_1[25:0];
  assign Offset = in_1[15:0];
  assign Opcode = in_1[31:26];
  assign RD = in_1[15:11];
  assign RS = in_1[25:21];
  assign RT = in_1[20:16];
  assign Shamt = in_1[10:6];

  // Notes on the sheet:
  //   R
endmodule

module mostrar (
  input  [5:0] in_1,
  output r,
  output add,
  output load,
  output store,
  output branch,
  output Jump
);

  Comparator #(.width(6)) comparator_1 (.a(in_1), .b({6{1'b0}}), .eq(r));  // open: gt, lt
  Comparator #(.width(6)) comparator_2 (.a(in_1), .b({6{1'b0}}), .eq(add));  // open: gt, lt
  Comparator #(.width(6)) comparator_3 (.a(in_1), .b(6'b100011), .eq(load));  // open: gt, lt
  Comparator #(.width(6)) comparator_4 (.a(in_1), .b(6'b101011), .eq(store));  // open: gt, lt
  Comparator #(.width(6)) comparator_5 (.a(in_1), .b(6'b100011), .eq(branch));  // open: gt, lt
  Comparator #(.width(6)) comparator_6 (.a(in_1), .b(6'b000010), .eq(Jump));  // open: gt, lt
endmodule

module Unidad_de_Registros (
  input  reset,
  input  clk,
  input  [4:0] rs,
  input  [4:0] rt,
  input  [4:0] rw,
  input  [31:0] Result,
  output [31:0] dato_1,
  output [31:0] dato_2
);

  wire a0, a1, a2, a3, a4, a5, a6, a7, a8, a9, a10, a11, a12, a13, a14, a15, a16, a17, a18, a19, a20, a21,
       a22, a23, a24, a25, a26, a27, a28, a29, a30, a31, undriven;
  wire [31:0] _0, _1, _2, _3, _4, _5, _6, _7, _8, _9, _10, _11, _12, _13, _14, _15, _16, _17, _18, _19, _20,
       _21, _22, _23, _24, _25, _26, _27, _28, _29, _30, _31, R0, R1, R2, R3, R4, R5, R6, R7, R8, R9, R10,
       R11, R12, R13, R14, R15, R16, R17, R18, R19, R20, R21, R22, R23, R24, R25, R26, R27, R28, R29, R30,
       R31;

  Register #(.width(32)) register_1 (.D(_15), .en(a15), .Q(R15), .clk(clk), .clr(reset));
  Register #(.width(32)) register_2 (.D(_16), .en(a16), .Q(R16), .clk(clk), .clr(reset));
  Register #(.width(32)) register_3 (.D(_17), .en(a17), .Q(R17), .clk(clk), .clr(reset));
  Register #(.width(32)) register_4 (.D(_18), .en(a18), .Q(R18), .clk(clk), .clr(reset));
  Register #(.width(32)) register_5 (.D(_19), .en(a19), .Q(R19), .clk(clk), .clr(reset));
  Register #(.width(32)) register_6 (.D(_20), .en(a20), .Q(R20), .clk(clk), .clr(reset));
  Register #(.width(32)) register_7 (.D(_21), .en(a21), .Q(R21), .clk(clk), .clr(reset));
  Register #(.width(32)) register_8 (.D(_22), .en(a22), .Q(R22), .clk(clk), .clr(reset));
  Register #(.width(32)) register_9 (.D(_23), .en(a23), .Q(R23), .clk(clk), .clr(reset));
  Register #(.width(32)) register_10 (.D(_24), .en(a24), .Q(R24), .clk(clk), .clr(reset));
  Register #(.width(32)) register_11 (.D(_25), .en(a25), .Q(R25), .clk(clk), .clr(reset));
  Register #(.width(32)) register_12 (.D(_26), .en(a26), .Q(R26), .clk(clk), .clr(reset));
  Register #(.width(32)) register_13 (.D(_27), .en(a27), .Q(R27), .clk(clk), .clr(reset));
  Register #(.width(32)) register_14 (.D(_28), .en(a28), .Q(R28), .clk(clk), .clr(reset));
  Register #(.width(32)) register_15 (.D(_29), .en(a29), .Q(R29), .clk(clk), .clr(reset));
  Register #(.width(32)) register_16 (.D(_30), .en(a30), .Q(R30), .clk(clk), .clr(reset));
  Register #(.width(32)) register_17 (.D(_31), .en(a31), .Q(R31), .clk(clk), .clr(reset));
  Register #(.width(32)) register_18 (.D(_0), .en(a0), .Q(R0), .clk(clk), .clr(reset));
  Register #(.width(32)) register_19 (.D(_1), .en(a1), .Q(R1), .clk(clk), .clr(reset));
  Register #(.width(32)) register_20 (.D(_2), .en(a2), .Q(R2), .clk(clk), .clr(reset));
  Register #(.width(32)) register_21 (.D(_3), .en(a3), .Q(R3), .clk(clk), .clr(reset));
  Register #(.width(32)) register_22 (.D(_4), .en(a4), .Q(R4), .clk(clk), .clr(reset));
  Register #(.width(32)) register_23 (.D(_5), .en(a5), .Q(R5), .clk(clk), .clr(reset));
  Register #(.width(32)) register_24 (.D(_6), .en(a6), .Q(R6), .clk(clk), .clr(reset));
  Register #(.width(32)) register_25 (.D(_7), .en(a7), .Q(R7), .clk(clk), .clr(reset));
  Register #(.width(32)) register_26 (.D(_8), .en(a8), .Q(R8), .clk(clk), .clr(reset));
  Register #(.width(32)) register_27 (.D(_9), .en(a9), .Q(R9), .clk(clk), .clr(reset));
  Register #(.width(32)) register_28 (.D(_10), .en(a10), .Q(R10), .clk(clk), .clr(reset));
  Register #(.width(32)) register_29 (.D(_11), .en(a11), .Q(R11), .clk(clk), .clr(reset));
  Register #(.width(32)) register_30 (.D(_12), .en(a12), .Q(R12), .clk(clk), .clr(reset));
  Register #(.width(32)) register_31 (.D(_13), .en(a13), .Q(R13), .clk(clk), .clr(reset));
  Register #(.width(32)) register_32 (.D(_14), .en(a14), .Q(R14), .clk(clk), .clr(reset));
  Multiplexer #(.select(5), .width(32)) multiplexer_1 (
    .in0(R0), .in1(R1), .in2(R2), .in3(R3), .in4(R4), .in5(R5), .in6(R6), .in7(R7), .in8(R8), .in9(R9),
    .in10(R10), .in11(R11), .in12(R12), .in13(R13), .in14(R14), .in15(R15), .in16(R16), .in17(R17),
    .in18(R18), .in19(R19), .in20(R20), .in21(R21), .in22(R22), .in23(R23), .in24(R24), .in25(R25),
    .in26(R26), .in27(R27), .in28(R28), .in29(R29), .in30(R30), .in31(R31), .out(dato_1), .sel(rs));  // open: en
  Multiplexer #(.select(5), .width(32)) multiplexer_2 (
    .in0(R0), .in1(R1), .in2(R2), .in3(R3), .in4(R4), .in5(R5), .in6(R6), .in7(R7), .in8(R8), .in9(R9),
    .in10(R10), .in11(R11), .in12(R12), .in13(R13), .in14(R14), .in15(R15), .in16(R16), .in17(R17),
    .in18(R18), .in19(R19), .in20(R20), .in21(R21), .in22(R22), .in23(R23), .in24(R24), .in25(R25),
    .in26(R26), .in27(R27), .in28(R28), .in29(R29), .in30(R30), .in31(R31), .out(dato_2), .sel(rt),
    .en(undriven));
  Demultiplexer #(.select(5), .width(32)) demultiplexer_1 (
    .out0(_0), .out1(_1), .out2(_2), .out3(_3), .out4(_4), .out5(_5), .out6(_6), .out7(_7), .out8(_8),
    .out9(_9), .out10(_10), .out11(_11), .out12(_12), .out13(_13), .out14(_14), .out15(_15), .out16(_16),
    .out17(_17), .out18(_18), .out19(_19), .out20(_20), .out21(_21), .out22(_22), .out23(_23), .out24(_24),
    .out25(_25), .out26(_26), .out27(_27), .out28(_28), .out29(_29), .out30(_30), .out31(_31), .in(Result),
    .sel(rw));  // open: en
  Demultiplexer #(.select(5)) demultiplexer_2 (
    .out0(a0), .out1(a1), .out2(a2), .out3(a3), .out4(a4), .out5(a5), .out6(a6), .out7(a7), .out8(a8),
    .out9(a9), .out10(a10), .out11(a11), .out12(a12), .out13(a13), .out14(a14), .out15(a15), .out16(a16),
    .out17(a17), .out18(a18), .out19(a19), .out20(a20), .out21(a21), .out22(a22), .out23(a23), .out24(a24),
    .out25(a25), .out26(a26), .out27(a27), .out28(a28), .out29(a29), .out30(a30), .out31(a31), .in(1'b1),
    .sel(rw));  // open: en

  // Other names for the same wires on the sheet: clock = clk; Direccion1[4:0] = rs; Direccion2[4:0] = rt;
  //   Direccion3[4:0] = rw; Direccion4[31:0] = Result
endmodule

module depende (
  input  [5:0] in_1,
  output r,
  output add
);

  Comparator #(.width(6)) comparator_1 (.a(in_1), .b({6{1'b0}}), .eq(r));  // open: gt, lt
  Comparator #(.width(6)) comparator_2 (.a(in_1), .b(6'b001000), .eq(add));  // open: gt, lt
endmodule
