// Logisim project CPU_Pipeline.circ as structural Verilog: 26 circuits, main circuit main
module main (
  output [3:0] Selec_de_ALU
);

  wire add, addi, alu_1_zero, and_1_out, and_2_out, brach, clock, comparator_1_eq, comparator_2_eq,
       comparator_2_gt, des_ex_1_alusrc_out, des_ex_1_branch_out, des_ex_1_cost, des_ex_1_jump_sel_out,
       des_ex_1_memread_out, des_ex_1_memtoreg_out, des_ex_1_memwrite_out, des_ex_1_regwrite_out,
       ex_mem_1_alusrc_out, ex_mem_1_branch_out, ex_mem_1_cost, ex_mem_1_jump_sel_out, ex_mem_1_memread_out,
       ex_mem_1_memtoreg_out, ex_mem_1_memwrite_out, ex_mem_1_regwrite_out, ex_mem_1_zero_out,
       forwarding_unit_1_hazard, Jump, load, mem_wr_1_alusrc_out, mem_wr_1_cost, mem_wr_1_memtoreg_out,
       mem_wr_1_regwrite_out, not_1_out, or_1_out, or_2_out, Reset, stall, store, type_inst_1_r, undriven;
  wire [1:0] ALUop, forwarding_unit_1_forwarda, forwarding_unit_1_forwardb;
  wire [3:0] des_ex_1_selec_de_alu_out, dis_1_dec, dis_1_unit, dis_2_dec, dis_2_unit, dis_3_dec, dis_3_unit,
       dis_4_dec, dis_4_unit, ex_mem_1_selec_de_alu_out, mem_wr_1_selec_de_alu_out;
  wire [4:0] decodificador_1_rd, decodificador_1_rs, decodificador_1_rt, des_ex_1_rd_out, des_ex_1_rs_out,
       des_ex_1_rt_out, ex_mem_1_rd_out, ex_mem_1_rs_out, ex_mem_1_rt_out, ex_mem_1_rw_out, mem_wr_1_rw_out,
       multiplexer_8_out;
  wire [5:0] decodificador_1_opcode, des_ex_1_out_45, ex_mem_1_opcode_2, Funct, mem_wr_1_out_30;
  wire [6:0] uc_1_regdst;
  wire [8:0] des_ex_1_opcoderesult_2, ex_mem_1_opcoderesult_2, mem_wr_1_opcoderesult_2, multiplexer_3_out;
  wire [14:0] multiplexer_5_out;
  wire [15:0] decodificador_1_offset;
  wire [23:0] bit_extender_1_out, bit_extender_3_out, bit_extender_5_out, des_ex_1_pc_1_out, des_ex_1_pc_out,
       ex_mem_1_pc_branch_out, ex_mem_1_pc_out, if_dec_1_pc_1_out, mem_wr_1_pc_out, multiplexer_1_out,
       multiplexer_2_out, pc_1, pc_brach_1_pc_brach;
  wire [24:0] if_dec_1_pc_out, multiplexer_4_out;
  wire [25:0] decodificador_1_jump, des_ex_1_jump_out, ex_mem_1_jump_out;
  wire [31:0] alu_1_result, bit_extender_2_out, bit_extender_4_out, des_ex_1_offset_out, des_ex_1_r1_out,
       des_ex_1_r2_out, ex_mem_1_r2_out, ex_mem_1_ra_out, if_dec_1_instruccion_in_2, matriz_typeinstu_1_m0,
       matriz_typeinstu_1_m1, matriz_typeinstu_1_r0, matriz_typeinstu_1_r1, matriz_typeinstu_1_r2,
       matriz_typeinstu_1_r3, matriz_typeinstu_1_r4, matriz_typeinstu_2_m0, matriz_typeinstu_2_m1,
       matriz_typeinstu_2_r0, matriz_typeinstu_2_r1, matriz_typeinstu_2_r2, matriz_typeinstu_2_r3,
       matriz_typeinstu_2_r4, matriz_typeinstu_3_m0, matriz_typeinstu_3_m1, matriz_typeinstu_3_r0,
       matriz_typeinstu_3_r1, matriz_typeinstu_3_r2, matriz_typeinstu_3_r3, matriz_typeinstu_3_r4,
       matriz_typeinstu_4_m0, matriz_typeinstu_4_m1, matriz_typeinstu_4_r0, matriz_typeinstu_4_r1,
       matriz_typeinstu_4_r2, matriz_typeinstu_4_r3, matriz_typeinstu_4_r4, mem_wr_1_do_out, mem_wr_1_ra_out,
       multiplexer_6_out, multiplexer_7_out, multiplexer_9_out, multiplexer_10_out, PC_q, ram_1_data,
       ram_2_data, unidad_de_registros_1_dato_1, unidad_de_registros_1_dato_2;

  Multiplexer #(.width(24)) multiplexer_1 (
    .in0(pc_1), .in1(ex_mem_1_pc_branch_out), .out(multiplexer_1_out), .sel(and_2_out));  // open: en
  Bit_Extender #(.in_width(26), .out_width(24)) bit_extender_1 (.in(ex_mem_1_jump_out), .out(bit_extender_1_out));
  Multiplexer #(.width(24)) multiplexer_2 (
    .in0(multiplexer_1_out), .in1(bit_extender_1_out), .out(multiplexer_2_out), .sel(ex_mem_1_jump_sel_out));  // open: en
  Register #(.width(32)) PC (.D(bit_extender_2_out), .en(stall), .Q(PC_q), .clk(clock), .clr(Reset));
  assign bit_extender_2_out = {{8{1'b0}}, multiplexer_2_out};  // Bit_Extender bit_extender_2
  Bit_Extender #(.in_width(32), .out_width(24)) bit_extender_3 (.in(PC_q), .out(bit_extender_3_out));
  Adder #(.width(24)) adder_1 (.a(24'h1), .b(bit_extender_3_out), .out(pc_1));  // open: cin, cout
  Clock clock_1 (.out(clock));
  Button button_1 (.out(Reset));
  Comparator #(.width(32)) comparator_1 (.a(ram_1_data), .b({32{1'b0}}), .eq(comparator_1_eq));  // open: gt, lt
  or or_1 (or_1_out, comparator_2_gt, comparator_2_eq);
  Comparator #(.width(24)) comparator_2 (
    .a(bit_extender_3_out), .b({24{1'b0}}), .gt(comparator_2_gt), .eq(comparator_2_eq));  // open: lt
  RAM #(.addrWidth(24), .dataWidth(32)) ram_1 (
    .addr(bit_extender_3_out), .data(ram_1_data));  // open: sel, clk, ld, clr
  and and_1 (and_1_out, ~comparator_1_eq, or_1_out);  // AND_Gate
  IF_DEC if_dec_1 (
    .clk(clock), .pc_1_in(pc_1), .instruccion_in(ram_1_data), .reset(Reset), .pc_1_out(if_dec_1_pc_1_out),
    .pc_in(bit_extender_3_out), .pc_out(if_dec_1_pc_out[23:0]), .instruccion_in_2(if_dec_1_instruccion_in_2),
    .enable(stall), .\const (and_1_out), .cost(if_dec_1_pc_out[24]));
  UC uc_1 (
    .OpCode(decodificador_1_opcode), .RegDst(uc_1_regdst[0]), .ALUsrc(addi), .MemToReg(uc_1_regdst[2]),
    .RegWrite(uc_1_regdst[3]), .MemRead(uc_1_regdst[4]), .MemWrite(uc_1_regdst[5]), .Branch(uc_1_regdst[6]),
    .ALUOp(ALUop));
  Decodificador decodificador_1 (
    .Instruccion(if_dec_1_instruccion_in_2), .Funct(Funct), .RD(decodificador_1_rd), .RT(decodificador_1_rt),
    .RS(decodificador_1_rs), .Opcode(decodificador_1_opcode), .Offset(decodificador_1_offset),
    .Jump(decodificador_1_jump));  // open: Shamt
  type_Inst type_inst_1 (
    .in_1(decodificador_1_opcode), .r(type_inst_1_r), .add(add), .load(load), .store(store), .branch(brach),
    .Jump(Jump));
  LED r (.in(type_inst_1_r));
  matriz_typeInstu matriz_typeinstu_1 (
    .addi(addi), .r0(matriz_typeinstu_1_r0), .m0(matriz_typeinstu_1_m0), .r1(matriz_typeinstu_1_r1),
    .m1(matriz_typeinstu_1_m1), .r2(matriz_typeinstu_1_r2), .r3(matriz_typeinstu_1_r3),
    .r4(matriz_typeinstu_1_r4), .Opcode(decodificador_1_opcode), .cnst(if_dec_1_pc_out[24]),
    .alu_SEL(Selec_de_ALU), .in_5({ALUop, uc_1_regdst[6:2], addi, uc_1_regdst[0]}));
  DotMatrix #(.inputtype("row"), .matrixcols(32), .matrixrows(5)) dotmatrix_1 (
    .row0(matriz_typeinstu_1_r0), .row1(matriz_typeinstu_1_r1), .row2(matriz_typeinstu_1_r2),
    .row3(matriz_typeinstu_1_r3), .row4(matriz_typeinstu_1_r4));
  DotMatrix #(.inputtype("row"), .matrixcols(32), .matrixrows(2), .dotshape("circle")) dotmatrix_2 (
    .row0(matriz_typeinstu_1_m0), .row1(matriz_typeinstu_1_m1));
  DIS dis_1 (.CONST(if_dec_1_pc_out[24]), .PC(if_dec_1_pc_out[23:0]), .DEC(dis_1_dec), .UNIT(dis_1_unit));
  LED led_1 (.in(Jump));
  ALUcontrol alucontrol_1 (.ALUOp(ALUop), .funct(Funct), .out_3(Selec_de_ALU));
  LED led_2 (.in(add));
  LED led_3 (.in(load));
  LED led_4 (.in(store));
  LED led_5 (.in(brach));
  Multiplexer #(.width(9)) multiplexer_3 (
    .in0({9{1'b0}}), .in1({ALUop, uc_1_regdst[6:2], addi, uc_1_regdst[0]}), .out(multiplexer_3_out),
    .sel(stall));  // open: en
  Multiplexer #(.width(25)) multiplexer_4 (
    .in0({25{1'b0}}), .in1(if_dec_1_pc_out), .out(multiplexer_4_out), .sel(stall));  // open: en
  Hazard_detection_unit hazard_detection_unit_1 (
    .ID_EX_MemRead(des_ex_1_memread_out), .ID_EX_RegisterRt(des_ex_1_rt_out),
    .IF_ID_RegisterRs(decodificador_1_rs), .IF_ID_RegisterRT(decodificador_1_rt), .Stall(stall));
  assign bit_extender_4_out = {{16{1'b0}}, decodificador_1_offset};  // Bit_Extender bit_extender_4
  Hex_Digit_Display hex_digit_display_1 (.value(dis_1_dec));  // open: dp
  not not_1 (not_1_out, clock);
  Multiplexer #(.width(15)) multiplexer_5 (
    .in0({15{1'b0}}), .in1({decodificador_1_rt, decodificador_1_rd, decodificador_1_rs}),
    .out(multiplexer_5_out), .sel(stall));  // open: en
  Hex_Digit_Display hex_digit_display_2 (.value(dis_1_unit));  // open: dp
  Unidad_de_Registros unidad_de_registros_1 (
    .reset(Reset), .clk(not_1_out), .rs(decodificador_1_rs), .rt(decodificador_1_rt), .rw(mem_wr_1_rw_out),
    .Result(multiplexer_10_out), .dato_1(unidad_de_registros_1_dato_1),
    .dato_2(unidad_de_registros_1_dato_2), .Regwrite(mem_wr_1_regwrite_out));
  DES_EX des_ex_1 (
    .clk(clock), .pc_1_in(if_dec_1_pc_1_out), .pc_1_out(des_ex_1_pc_1_out),
    .R1_in(unidad_de_registros_1_dato_1), .R1_out(des_ex_1_r1_out), .R2_in(unidad_de_registros_1_dato_2),
    .R2_out(des_ex_1_r2_out), .rd_in(multiplexer_5_out[9:5]), .rd_out(des_ex_1_rd_out),
    .rt_in(multiplexer_5_out[14:10]), .rt_out(des_ex_1_rt_out), .pc_in(multiplexer_4_out[23:0]),
    .pc_out(des_ex_1_pc_out), .offset_in(bit_extender_4_out), .offset_out(des_ex_1_offset_out),
    .RegDst_in(multiplexer_3_out[0]), .ALUsrc_in(multiplexer_3_out[1]), .MemToReg_in(multiplexer_3_out[2]),
    .RegWrite_in(multiplexer_3_out[3]), .MemRead_in(multiplexer_3_out[4]),
    .MemWrite_in(multiplexer_3_out[5]), .Branch_in(multiplexer_3_out[6]), .ALUOp_in(multiplexer_3_out[8:7]),
    .ALUsrc_out(des_ex_1_alusrc_out), .MemToReg_out(des_ex_1_memtoreg_out),
    .RegWrite_out(des_ex_1_regwrite_out), .MemRead_out(des_ex_1_memread_out),
    .MemWrite_out(des_ex_1_memwrite_out), .Branch_out(des_ex_1_branch_out), .Selec_de_ALU_in(Selec_de_ALU),
    .Selec_de_ALU_out(des_ex_1_selec_de_alu_out), .jum_Sel_in(Jump), .Jump_in(decodificador_1_jump),
    .Jump_out(des_ex_1_jump_out), .jump_sel_out(des_ex_1_jump_sel_out), .rs_in(multiplexer_5_out[4:0]),
    .rs_out(des_ex_1_rs_out), .in_22(decodificador_1_opcode), .out_45(des_ex_1_out_45), .enable(1'b1),
    .reset(Reset), .\const (multiplexer_4_out[24]), .cost(des_ex_1_cost), .opcoderesult(multiplexer_3_out),
    .opcoderesult_2(des_ex_1_opcoderesult_2));  // open: RegDst_out, ALUOp_out
  matriz_typeInstu matriz_typeinstu_2 (
    .addi(des_ex_1_alusrc_out), .r0(matriz_typeinstu_2_r0), .m0(matriz_typeinstu_2_m0),
    .r1(matriz_typeinstu_2_r1), .m1(matriz_typeinstu_2_m1), .r2(matriz_typeinstu_2_r2),
    .r3(matriz_typeinstu_2_r3), .r4(matriz_typeinstu_2_r4), .Opcode(des_ex_1_out_45), .cnst(des_ex_1_cost),
    .alu_SEL(des_ex_1_selec_de_alu_out), .in_5(des_ex_1_opcoderesult_2));
  DotMatrix #(.inputtype("row"), .matrixcols(32), .matrixrows(5)) dotmatrix_3 (
    .row0(matriz_typeinstu_2_r0), .row1(matriz_typeinstu_2_r1), .row2(matriz_typeinstu_2_r2),
    .row3(matriz_typeinstu_2_r3), .row4(matriz_typeinstu_2_r4));
  DotMatrix #(.inputtype("row"), .matrixcols(32), .matrixrows(2), .dotshape("circle")) dotmatrix_4 (
    .row0(matriz_typeinstu_2_m0), .row1(matriz_typeinstu_2_m1));
  DIS dis_2 (.CONST(des_ex_1_cost), .PC(des_ex_1_pc_out), .DEC(dis_2_dec), .UNIT(dis_2_unit));
  Multiplexer #(.select(2), .width(32)) multiplexer_6 (
    .in0(des_ex_1_r1_out), .in1(multiplexer_10_out), .in2(ex_mem_1_ra_out), .out(multiplexer_6_out),
    .sel(forwarding_unit_1_forwarda));  // open: in3, en
  Multiplexer #(.select(2), .width(32)) multiplexer_7 (
    .in0(des_ex_1_r2_out), .in1(multiplexer_10_out), .in2(ex_mem_1_ra_out), .out(multiplexer_7_out),
    .sel(forwarding_unit_1_forwardb), .en(undriven));  // open: in3
  Multiplexer #(.width(5)) multiplexer_8 (
    .in0(des_ex_1_rd_out), .in1(des_ex_1_rt_out), .out(multiplexer_8_out), .sel(des_ex_1_alusrc_out));  // open: en
  Pc_brach pc_brach_1 (.pc_1(des_ex_1_pc_1_out), .offset(des_ex_1_offset_out), .pc_brach(pc_brach_1_pc_brach));
  Forwarding_unit forwarding_unit_1 (
    .EX_MEM_RegWrite(ex_mem_1_regwrite_out), .EX_MEM_Rd(ex_mem_1_rw_out), .ID_EX_Rt(des_ex_1_rt_out),
    .ID_EX_Rs(des_ex_1_rs_out), .MEM_WB_RegWr(mem_wr_1_regwrite_out), .MEM_WB_Rd(mem_wr_1_rw_out),
    .ForwardA(forwarding_unit_1_forwarda), .ForwardB(forwarding_unit_1_forwardb),
    .hazard(forwarding_unit_1_hazard));
  Multiplexer #(.width(32)) multiplexer_9 (
    .in0(multiplexer_7_out), .in1(des_ex_1_offset_out), .out(multiplexer_9_out), .sel(des_ex_1_alusrc_out));  // open: en
  EX_MEM ex_mem_1 (
    .pc_brach_in(pc_brach_1_pc_brach), .pc_branch_out(ex_mem_1_pc_branch_out), .ZERO_in(alu_1_zero),
    .ZERO_out(ex_mem_1_zero_out), .clk(clock), .reset(Reset), .RA_in(alu_1_result), .RA_out(ex_mem_1_ra_out),
    .R2_in(multiplexer_7_out), .R2_out(ex_mem_1_r2_out), .RW_in(multiplexer_8_out), .RW_out(ex_mem_1_rw_out),
    .pc_in(des_ex_1_pc_out), .pc_out(ex_mem_1_pc_out), .MemToReg_in(des_ex_1_memtoreg_out),
    .MemToReg_out(ex_mem_1_memtoreg_out), .RegWrite_in(des_ex_1_regwrite_out),
    .RegWrite_out(ex_mem_1_regwrite_out), .MemRead_in(des_ex_1_memread_out),
    .MemRead_out(ex_mem_1_memread_out), .MemWrite_in(des_ex_1_memwrite_out),
    .MemWrite_out(ex_mem_1_memwrite_out), .Branch_in(des_ex_1_branch_out), .Branch_out(ex_mem_1_branch_out),
    .Jump_in(des_ex_1_jump_out), .Jump_out(ex_mem_1_jump_out), .jum_Sel_in(des_ex_1_jump_sel_out),
    .jump_sel_out(ex_mem_1_jump_sel_out), .rs_in(des_ex_1_rs_out), .rs_out(ex_mem_1_rs_out),
    .rd_in(des_ex_1_rd_out), .rd_out(ex_mem_1_rd_out), .rt_in(des_ex_1_rt_out), .rt_out(ex_mem_1_rt_out),
    .opcode(des_ex_1_out_45), .opcode_2(ex_mem_1_opcode_2), .ALUsrc_in(des_ex_1_alusrc_out),
    .ALUsrc_out(ex_mem_1_alusrc_out), .ena(1'b1), .\const (des_ex_1_cost), .cost(ex_mem_1_cost),
    .Selec_de_ALU_in(des_ex_1_selec_de_alu_out), .Selec_de_ALU_out(ex_mem_1_selec_de_alu_out),
    .opcoderesult(des_ex_1_opcoderesult_2), .opcoderesult_2(ex_mem_1_opcoderesult_2));
  ALU alu_1 (
    .DATA1(multiplexer_6_out), .DATA2(multiplexer_9_out), .AluControl(des_ex_1_selec_de_alu_out),
    .RESULT(alu_1_result), .Zero(alu_1_zero));
  Hex_Digit_Display hex_digit_display_3 (.value(dis_2_dec));  // open: dp
  Hex_Digit_Display hex_digit_display_4 (.value(dis_2_unit));  // open: dp
  and and_2 (and_2_out, ex_mem_1_branch_out, ex_mem_1_zero_out);
  matriz_typeInstu matriz_typeinstu_3 (
    .addi(ex_mem_1_alusrc_out), .r0(matriz_typeinstu_3_r0), .m0(matriz_typeinstu_3_m0),
    .r1(matriz_typeinstu_3_r1), .m1(matriz_typeinstu_3_m1), .r2(matriz_typeinstu_3_r2),
    .r3(matriz_typeinstu_3_r3), .r4(matriz_typeinstu_3_r4), .Opcode(ex_mem_1_opcode_2), .cnst(ex_mem_1_cost),
    .alu_SEL(ex_mem_1_selec_de_alu_out), .in_5(ex_mem_1_opcoderesult_2));
  DotMatrix #(.inputtype("row"), .matrixcols(32), .matrixrows(5)) dotmatrix_5 (
    .row0(matriz_typeinstu_3_r0), .row1(matriz_typeinstu_3_r1), .row2(matriz_typeinstu_3_r2),
    .row3(matriz_typeinstu_3_r3), .row4(matriz_typeinstu_3_r4));
  DotMatrix #(.inputtype("row"), .matrixcols(32), .matrixrows(2), .dotshape("circle")) dotmatrix_6 (
    .row0(matriz_typeinstu_3_m0), .row1(matriz_typeinstu_3_m1));
  DIS dis_3 (.CONST(ex_mem_1_cost), .PC(ex_mem_1_pc_out), .DEC(dis_3_dec), .UNIT(dis_3_unit));
  Bit_Extender #(.in_width(32), .out_width(24)) bit_extender_5 (.in(ex_mem_1_ra_out), .out(bit_extender_5_out));
  or or_2 (or_2_out, ex_mem_1_memwrite_out, ex_mem_1_memread_out);
  RAM #(.addrWidth(24), .dataWidth(32), .bus("separate")) ram_2 (
    .addr(bit_extender_5_out), .din(ex_mem_1_r2_out), .data(ram_2_data), .sel(or_2_out), .clk(clock),
    .ld(ex_mem_1_memread_out), .clr(Reset));  // open: str
  Mem_Wr mem_wr_1 (
    .RA_in(ex_mem_1_ra_out), .RA_out(mem_wr_1_ra_out), .DO_in(ram_2_data), .DO_out(mem_wr_1_do_out),
    .RW_in(ex_mem_1_rw_out), .RW_out(mem_wr_1_rw_out), .pc_in(ex_mem_1_pc_out), .pc_out(mem_wr_1_pc_out),
    .MemToReg_in(ex_mem_1_memtoreg_out), .MemToReg_out(mem_wr_1_memtoreg_out),
    .RegWrite_in(ex_mem_1_regwrite_out), .RegWrite_out(mem_wr_1_regwrite_out),
    .MemRead_in(ex_mem_1_memread_out), .rs_in(ex_mem_1_rs_out), .rd_in(ex_mem_1_rd_out),
    .rt_in(ex_mem_1_rt_out), .opcode(ex_mem_1_opcode_2), .out_30(mem_wr_1_out_30),
    .ALUsrc_in(ex_mem_1_alusrc_out), .ALUsrc_out(mem_wr_1_alusrc_out), .clk(clock), .reset(Reset),
    .ENABLEhAZAR(forwarding_unit_1_hazard), .\const (ex_mem_1_cost), .cost(mem_wr_1_cost),
    .Selec_de_ALU_in(ex_mem_1_selec_de_alu_out), .Selec_de_ALU_out(mem_wr_1_selec_de_alu_out),
    .opcoderesult(ex_mem_1_opcoderesult_2), .opcoderesult_2(mem_wr_1_opcoderesult_2));  // open: MemRead_out, rs_out, rd_out, rt_out, ENABLE
  Hex_Digit_Display hex_digit_display_5 (.value(dis_3_unit));  // open: dp
  Hex_Digit_Display hex_digit_display_6 (.value(dis_3_dec));  // open: dp
  Multiplexer #(.width(32)) multiplexer_10 (
    .in0(mem_wr_1_ra_out), .in1(mem_wr_1_do_out), .out(multiplexer_10_out), .sel(mem_wr_1_memtoreg_out));  // open: en
  DotMatrix #(.inputtype("row"), .matrixcols(32), .matrixrows(5)) dotmatrix_7 (
    .row0(matriz_typeinstu_4_r0), .row1(matriz_typeinstu_4_r1), .row2(matriz_typeinstu_4_r2),
    .row3(matriz_typeinstu_4_r3), .row4(matriz_typeinstu_4_r4));
  matriz_typeInstu matriz_typeinstu_4 (
    .addi(mem_wr_1_alusrc_out), .r0(matriz_typeinstu_4_r0), .m0(matriz_typeinstu_4_m0),
    .r1(matriz_typeinstu_4_r1), .m1(matriz_typeinstu_4_m1), .r2(matriz_typeinstu_4_r2),
    .r3(matriz_typeinstu_4_r3), .r4(matriz_typeinstu_4_r4), .Opcode(mem_wr_1_out_30), .cnst(mem_wr_1_cost),
    .alu_SEL(mem_wr_1_selec_de_alu_out), .in_5(mem_wr_1_opcoderesult_2));
  DotMatrix #(.inputtype("row"), .matrixcols(32), .matrixrows(2), .dotshape("circle")) dotmatrix_8 (
    .row0(matriz_typeinstu_4_m0), .row1(matriz_typeinstu_4_m1));
  DIS dis_4 (.CONST(mem_wr_1_cost), .PC(mem_wr_1_pc_out), .DEC(dis_4_dec), .UNIT(dis_4_unit));
  Hex_Digit_Display hex_digit_display_7 (.value(dis_4_unit));  // open: dp
  Hex_Digit_Display hex_digit_display_8 (.value(dis_4_dec));  // open: dp

  // Notes on the sheet:
  //   La instruccion que esta en decode es:
endmodule

module Decodificador (
  input  [31:0] Instruccion,
  output [5:0] Funct,
  output [4:0] Shamt,
  output [4:0] RD,
  output [4:0] RT,
  output [4:0] RS,
  output [5:0] Opcode,
  output [15:0] Offset,
  output [25:0] Jump
);


  assign Funct = Instruccion[5:0];
  assign Jump = Instruccion[25:0];
  assign Offset = Instruccion[15:0];
  assign Opcode = Instruccion[31:26];
  assign RD = Instruccion[15:11];
  assign RS = Instruccion[25:21];
  assign RT = Instruccion[20:16];
  assign Shamt = Instruccion[10:6];

  // Notes on the sheet:
  //   R
endmodule

module type_Inst (
  input  [5:0] in_1,
  output r,
  output add,
  output load,
  output store,
  output branch,
  output Jump
);

  Comparator #(.width(6)) comparator_1 (.a(in_1), .b({6{1'b0}}), .eq(r));  // open: gt, lt
  Comparator #(.width(6)) comparator_2 (.a(in_1), .b({6{1'b0}}), .eq(add));  // open: gt, lt
  Comparator #(.width(6)) comparator_3 (.a(in_1), .b(6'b100011), .eq(load));  // open: gt, lt
  Comparator #(.width(6)) comparator_4 (.a(in_1), .b(6'b101011), .eq(store));  // open: gt, lt
  Comparator #(.width(6)) comparator_5 (.a(in_1), .b(6'b000100), .eq(branch));  // open: gt, lt
  Comparator #(.width(6)) comparator_6 (.a(in_1), .b(6'b000010), .eq(Jump));  // open: gt, lt
endmodule

// Registros
module Unidad_de_Registros (
  input  reset,
  input  clk,
  input  [4:0] rs,
  input  Regwrite,
  input  [4:0] rt,
  input  [4:0] rw,
  input  [31:0] Result,
  output [31:0] dato_1,
  output [31:0] dato_2
);

  wire a0, a1, a2, a3, a4, a5, a6, a7, a8, a9, a10, a11, a12, a13, a14, a15, a16, a17, a18, a19, a20, a21,
       a22, a23, a24, a25, a26, a27, a28, a29, a30, a31, undriven;
  wire [31:0] R0, R1, R2, R3, R4, R5, R6, R7, R8, R9, R10, R11, R12, R13, R14, R15, R16, R17, R18, R19, R20,
       R21, R22, R23, R24, R25, R26, R27, R28, R29, R30, R31;

  Register #(.width(32)) register_1 (.D(Result), .en(a0), .Q(R0), .clk(clk), .clr(reset));
  Register #(.width(32)) register_2 (.D(Result), .en(a6), .Q(R6), .clk(clk), .clr(reset));
  Register #(.width(32)) register_3 (.D(Result), .en(a12), .Q(R12), .clk(clk), .clr(reset));
  Register #(.width(32)) register_4 (.D(Result), .en(a18), .Q(R18), .clk(clk), .clr(reset));
  Register #(.width(32)) register_5 (.D(Result), .en(a24), .Q(R24), .clk(clk), .clr(reset));
  Register #(.width(32)) register_6 (.D(Result), .en(a30), .Q(R30), .clk(clk), .clr(reset));
  // Probe on R12
  Multiplexer #(.select(5), .width(32)) multiplexer_1 (
    .in0(R0), .in1(R1), .in2(R2), .in3(R3), .in4(R4), .in5(R5), .in6(R6), .in7(R7), .in8(R8), .in9(R9),
    .in10(R10), .in11(R11), .in12(R12), .in13(R13), .in14(R14), .in15(R15), .in16(R16), .in17(R17),
    .in18(R18), .in19(R19), .in20(R20), .in21(R21), .in22(R22), .in23(R23), .in24(R24), .in25(R25),
    .in26(R26), .in27(R27), .in28(R28), .in29(R29), .in30(R30), .in31(R31), .out(dato_1), .sel(rs));  // open: en
  Register #(.width(32)) register_7 (.D(Result), .en(a1), .Q(R1), .clk(clk), .clr(reset));
  Register #(.width(32)) register_8 (.D(Result), .en(a7), .Q(R7), .clk(clk), .clr(reset));
  Register #(.width(32)) register_9 (.D(Result), .en(a13), .Q(R13), .clk(clk), .clr(reset));
  Register #(.width(32)) register_10 (.D(Result), .en(a19), .Q(R19), .clk(clk), .clr(reset));
  Register #(.width(32)) register_11 (.D(Result), .en(a25), .Q(R25), .clk(clk), .clr(reset));
  Register #(.width(32)) register_12 (.D(Result), .en(a31), .Q(R31), .clk(clk), .clr(reset));
  Register #(.width(32)) register_13 (.D(Result), .en(a2), .Q(R2), .clk(clk), .clr(reset));
  Register #(.width(32)) register_14 (.D(Result), .en(a8), .Q(R8), .clk(clk), .clr(reset));
  Register #(.width(32)) register_15 (.D(Result), .en(a14), .Q(R14), .clk(clk), .clr(reset));
  Register #(.width(32)) register_16 (.D(Result), .en(a20), .Q(R20), .clk(clk), .clr(reset));
  Register #(.width(32)) register_17 (.D(Result), .en(a26), .Q(R26), .clk(clk), .clr(reset));
  Multiplexer #(.select(5), .width(32)) multiplexer_2 (
    .in0(R0), .in1(R1), .in2(R2), .in3(R3), .in4(R4), .in5(R5), .in6(R6), .in7(R7), .in8(R8), .in9(R9),
    .in10(R10), .in11(R11), .in12(R12), .in13(R13), .in14(R14), .in15(R15), .in16(R16), .in17(R17),
    .in18(R18), .in19(R19), .in20(R20), .in21(R21), .in22(R22), .in23(R23), .in24(R24), .in25(R25),
    .in26(R26), .in27(R27), .in28(R28), .in29(R29), .in30(R30), .in31(R31), .out(dato_2), .sel(rt),
    .en(undriven));
  Register #(.width(32)) register_18 (.D(Result), .en(a3), .Q(R3), .clk(clk), .clr(reset));
  Register #(.width(32)) register_19 (.D(Result), .en(a9), .Q(R9), .clk(clk), .clr(reset));
  Register #(.width(32)) register_20 (.D(Result), .en(a15), .Q(R15), .clk(clk), .clr(reset));
  Register #(.width(32)) register_21 (.D(Result), .en(a21), .Q(R21), .clk(clk), .clr(reset));
  Register #(.width(32)) register_22 (.D(Result), .en(a27), .Q(R27), .clk(clk), .clr(reset));
  // Probe on R11
  Register #(.width(32)) register_23 (.D(Result), .en(a4), .Q(R4), .clk(clk), .clr(reset));
  Register #(.width(32)) register_24 (.D(Result), .en(a10), .Q(R10), .clk(clk), .clr(reset));
  Register #(.width(32)) register_25 (.D(Result), .en(a16), .Q(R16), .clk(clk), .clr(reset));
  Register #(.width(32)) register_26 (.D(Result), .en(a22), .Q(R22), .clk(clk), .clr(reset));
  Register #(.width(32)) register_27 (.D(Result), .en(a28), .Q(R28), .clk(clk), .clr(reset));
  Demultiplexer #(.select(5)) demultiplexer_1 (
    .out0(a0), .out1(a1), .out2(a2), .out3(a3), .out4(a4), .out5(a5), .out6(a6), .out7(a7), .out8(a8),
    .out9(a9), .out10(a10), .out11(a11), .out12(a12), .out13(a13), .out14(a14), .out15(a15), .out16(a16),
    .out17(a17), .out18(a18), .out19(a19), .out20(a20), .out21(a21), .out22(a22), .out23(a23), .out24(a24),
    .out25(a25), .out26(a26), .out27(a27), .out28(a28), .out29(a29), .out30(a30), .out31(a31), .in(Regwrite),
    .sel(rw));  // open: en
  Register #(.width(32)) register_28 (.D(Result), .en(a5), .Q(R5), .clk(clk), .clr(reset));
  Register #(.width(32)) register_29 (.D(Result), .en(a11), .Q(R11), .clk(clk), .clr(reset));
  Register #(.width(32)) register_30 (.D(Result), .en(a17), .Q(R17), .clk(clk), .clr(reset));
  Register #(.width(32)) register_31 (.D(Result), .en(a23), .Q(R23), .clk(clk), .clr(reset));
  Register #(.width(32)) register_32 (.D(Result), .en(a29), .Q(R29), .clk(clk), .clr(reset));

  // Other names for the same wires on the sheet: clock = clk; Direccion1[4:0] = rs; Direccion2[4:0] = rt;
  //   Direccion3[4:0] = rw; Direccion4[31:0] = Result
endmodule

module UCA (
  input  [1:0] ALUOp,
  input  [5:0] Func,
  output [3:0] out_3
);

  wire and_1_out, and_2_out, and_3_out, and_4_out, not_1_out, not_2_out, not_3_out;

  not not_1 (not_1_out, ALUOp[0]);
  not not_2 (not_2_out, ALUOp[0]);
  not not_3 (not_3_out, Func[2]);
  and and_1 (and_1_out, ALUOp[0], Func[0]);
  and and_2 (and_2_out, ALUOp[0], Func[3]);
  and and_3 (and_3_out, not_1_out, ALUOp[1]);
  and and_4 (and_4_out, ALUOp[0], Func[1]);
  or or_1 (out_3[1], not_2_out, not_3_out);
  or or_2 (out_3[0], and_1_out, and_2_out);
  or or_3 (out_3[2], and_3_out, and_4_out);

  assign out_3[3] = 1'b0;
endmodule

// UC
module UC (
  input  [5:0] OpCode,
  output RegDst,
  output ALUsrc,
  output MemToReg,
  output RegWrite,
  output MemRead,
  output MemWrite,
  output Branch,
  output [1:0] ALUOp
);

  wire and_2_out, and_3_out, not_2_out, not_3_out, not_4_out, not_5_out, not_6_out, not_7_out, not_8_out,
       not_9_out, not_10_out, not_11_out, not_12_out, not_13_out, not_14_out, not_15_out, not_16_out,
       not_17_out;

  not not_1 (RegDst, OpCode[5]);
  or or_1 (ALUsrc, OpCode[3], OpCode[1]);
  not not_2 (not_2_out, OpCode[2]);
  not not_3 (not_3_out, OpCode[3]);
  not not_4 (not_4_out, OpCode[2]);
  not not_5 (not_5_out, OpCode[5]);
  not not_6 (not_6_out, OpCode[3]);
  and and_1 (MemWrite, OpCode[0], OpCode[3]);
  not not_7 (not_7_out, OpCode[5]);
  not not_8 (not_8_out, OpCode[4]);
  not not_9 (not_9_out, OpCode[3]);
  not not_10 (not_10_out, OpCode[2]);
  not not_11 (not_11_out, OpCode[1]);
  not not_12 (not_12_out, OpCode[0]);
  not not_13 (not_13_out, OpCode[5]);
  not not_14 (not_14_out, OpCode[4]);
  not not_15 (not_15_out, OpCode[3]);
  not not_16 (not_16_out, OpCode[1]);
  not not_17 (not_17_out, OpCode[0]);
  and and_2 (and_2_out, not_2_out, not_3_out);
  and and_3 (and_3_out, not_4_out, not_5_out);
  and and_4 (MemRead, OpCode[1], not_6_out);
  or or_2 (RegWrite, and_2_out, and_3_out);
  and and_5 (ALUOp[1], not_7_out, not_8_out, not_9_out, not_10_out, not_11_out, not_12_out);
  and and_6 (ALUOp[0], not_13_out, not_14_out, not_15_out, OpCode[2], not_16_out, not_17_out);

  assign Branch = OpCode[2];
  assign MemToReg = OpCode[1];
endmodule

module IF_DEC (
  input  clk,
  input  reset,
  input  [23:0] pc_1_in,
  input  [31:0] instruccion_in,
  input  [23:0] pc_in,
  input  \const ,
  input  enable,
  output [23:0] pc_1_out,
  output [31:0] instruccion_in_2,
  output [23:0] pc_out,
  output cost
);

  Register #(.width(24)) register_1 (.D(pc_1_in), .en(enable), .Q(pc_1_out), .clk(clk), .clr(reset));
  Register #(.width(32)) register_2 (.D(instruccion_in), .en(enable), .Q(instruccion_in_2), .clk(clk), .clr(reset));
  Register #(.width(24)) register_3 (.D(pc_in), .en(enable), .Q(pc_out), .clk(clk), .clr(reset));
  Register #(.width(1)) register_4 (.D(\const ), .en(enable), .Q(cost), .clk(clk), .clr(reset));

  // Other names for the same wires on the sheet: ena = enable; res = reset
endmodule

module DES_EX (
  input  clk,
  input  reset,
  input  [23:0] pc_1_in,
  input  [31:0] R1_in,
  input  [31:0] R2_in,
  input  [31:0] offset_in,
  input  [4:0] rs_in,
  input  [4:0] rd_in,
  input  [4:0] rt_in,
  input  [23:0] pc_in,
  input  [25:0] Jump_in,
  input  jum_Sel_in,
  input  RegDst_in,
  input  ALUsrc_in,
  input  MemToReg_in,
  input  RegWrite_in,
  input  MemRead_in,
  input  MemWrite_in,
  input  Branch_in,
  input  [1:0] ALUOp_in,
  input  [3:0] Selec_de_ALU_in,
  input  [5:0] in_22,
  input  \const ,
  input  enable,
  input  [8:0] opcoderesult,
  output [23:0] pc_1_out,
  output [31:0] R1_out,
  output [31:0] R2_out,
  output [31:0] offset_out,
  output [4:0] rs_out,
  output [4:0] rd_out,
  output [4:0] rt_out,
  output [23:0] pc_out,
  output [25:0] Jump_out,
  output jump_sel_out,
  output RegDst_out,
  output ALUsrc_out,
  output MemToReg_out,
  output RegWrite_out,
  output MemRead_out,
  output MemWrite_out,
  output Branch_out,
  output [1:0] ALUOp_out,
  output [3:0] Selec_de_ALU_out,
  output [5:0] out_45,
  output cost,
  output [8:0] opcoderesult_2
);

  Register #(.width(1)) register_1 (.D(jum_Sel_in), .en(enable), .Q(jump_sel_out), .clk(clk), .clr(reset));
  Register #(.width(1)) register_2 (.D(\const ), .en(enable), .Q(cost), .clk(clk), .clr(reset));
  Register #(.width(24)) register_3 (.D(pc_1_in), .en(enable), .Q(pc_1_out), .clk(clk), .clr(reset));
  Register #(.width(32)) register_4 (.D(R1_in), .en(enable), .Q(R1_out), .clk(clk), .clr(reset));
  Register #(.width(32)) register_5 (.D(R2_in), .en(enable), .Q(R2_out), .clk(clk), .clr(reset));
  Register #(.width(32)) register_6 (.D(offset_in), .en(enable), .Q(offset_out), .clk(clk), .clr(reset));
  Register #(.width(5)) register_7 (.D(rs_in), .en(enable), .Q(rs_out), .clk(clk), .clr(reset));
  Register #(.width(5)) register_8 (.D(rd_in), .en(enable), .Q(rd_out), .clk(clk), .clr(reset));
  Register #(.width(5)) register_9 (.D(rt_in), .en(enable), .Q(rt_out), .clk(clk), .clr(reset));
  Register #(.width(24)) register_10 (.D(pc_in), .en(enable), .Q(pc_out), .clk(clk), .clr(reset));
  Register #(.width(26)) register_11 (.D(Jump_in), .en(enable), .Q(Jump_out), .clk(clk), .clr(reset));
  Register #(.width(1)) register_12 (.D(RegDst_in), .en(enable), .Q(RegDst_out), .clk(clk), .clr(reset));
  Register #(.width(1)) register_13 (.D(ALUsrc_in), .en(enable), .Q(ALUsrc_out), .clk(clk), .clr(reset));
  Register #(.width(1)) register_14 (.D(MemToReg_in), .en(enable), .Q(MemToReg_out), .clk(clk), .clr(reset));
  Register #(.width(1)) register_15 (.D(RegWrite_in), .en(enable), .Q(RegWrite_out), .clk(clk), .clr(reset));
  Register #(.width(1)) register_16 (.D(MemRead_in), .en(enable), .Q(MemRead_out), .clk(clk), .clr(reset));
  Register #(.width(1)) register_17 (.D(MemWrite_in), .en(enable), .Q(MemWrite_out), .clk(clk), .clr(reset));
  Register #(.width(1)) register_18 (.D(Branch_in), .en(enable), .Q(Branch_out), .clk(clk), .clr(reset));
  Register #(.width(2)) register_19 (.D(ALUOp_in), .en(enable), .Q(ALUOp_out), .clk(clk), .clr(reset));
  Register #(.width(4)) register_20 (.D(Selec_de_ALU_in), .en(enable), .Q(Selec_de_ALU_out), .clk(clk), .clr(reset));
  Register #(.width(6)) register_21 (.D(in_22), .en(enable), .Q(out_45), .clk(clk), .clr(reset));
  Register #(.width(9)) register_22 (.D(opcoderesult), .en(enable), .Q(opcoderesult_2), .clk(clk), .clr(reset));

  // Other names for the same wires on the sheet: res = reset
endmodule

module EX_MEM (
  input  clk,
  input  reset,
  input  ena,
  input  [23:0] pc_brach_in,
  input  ZERO_in,
  input  [31:0] RA_in,
  input  [31:0] R2_in,
  input  [4:0] RW_in,
  input  [4:0] rs_in,
  input  [4:0] rd_in,
  input  [4:0] rt_in,
  input  [23:0] pc_in,
  input  [25:0] Jump_in,
  input  jum_Sel_in,
  input  ALUsrc_in,
  input  MemToReg_in,
  input  RegWrite_in,
  input  MemRead_in,
  input  MemWrite_in,
  input  Branch_in,
  input  \const ,
  input  [5:0] opcode,
  input  [3:0] Selec_de_ALU_in,
  input  [8:0] opcoderesult,
  output [23:0] pc_branch_out,
  output ZERO_out,
  output [31:0] RA_out,
  output [31:0] R2_out,
  output [4:0] RW_out,
  output [4:0] rs_out,
  output [4:0] rd_out,
  output [4:0] rt_out,
  output [23:0] pc_out,
  output [25:0] Jump_out,
  output jump_sel_out,
  output ALUsrc_out,
  output MemToReg_out,
  output RegWrite_out,
  output MemRead_out,
  output MemWrite_out,
  output Branch_out,
  output cost,
  output [5:0] opcode_2,
  output [3:0] Selec_de_ALU_out,
  output [8:0] opcoderesult_2
);

  wire comparator_1_eq, resx;
  wire [1:0] counter_1_q;

  Register #(.width(1)) register_1 (.D(\const ), .en(ena), .Q(cost), .clk(clk), .clr(reset));
  Register #(.width(24)) register_2 (.D(pc_brach_in), .en(ena), .Q(pc_branch_out), .clk(clk), .clr(reset));
  Register #(.width(1)) register_3 (.D(ZERO_in), .en(ena), .Q(ZERO_out), .clk(clk), .clr(reset));
  Register #(.width(32)) register_4 (.D(RA_in), .en(ena), .Q(RA_out), .clk(clk), .clr(reset));
  Register #(.width(32)) register_5 (.D(R2_in), .en(ena), .Q(R2_out), .clk(clk), .clr(reset));
  Register #(.width(5)) register_6 (.D(RW_in), .en(ena), .Q(RW_out), .clk(clk), .clr(reset));
  Register #(.width(5)) register_7 (.D(rs_in), .en(ena), .Q(rs_out), .clk(clk), .clr(reset));
  Register #(.width(5)) register_8 (.D(rd_in), .en(ena), .Q(rd_out), .clk(clk), .clr(reset));
  Register #(.width(5)) register_9 (.D(rt_in), .en(ena), .Q(rt_out), .clk(clk), .clr(reset));
  Register #(.width(24)) register_10 (.D(pc_in), .en(ena), .Q(pc_out), .clk(clk), .clr(reset));
  Register #(.width(26)) register_11 (.D(Jump_in), .en(ena), .Q(Jump_out), .clk(clk), .clr(reset));
  Register #(.width(1)) register_12 (.D(jum_Sel_in), .en(ena), .Q(jump_sel_out), .clk(clk), .clr(reset));
  Register #(.width(1)) register_13 (.D(ALUsrc_in), .en(ena), .Q(ALUsrc_out), .clk(clk), .clr(reset));
  Register #(.width(1)) register_14 (.D(MemToReg_in), .en(ena), .Q(MemToReg_out), .clk(clk), .clr(reset));
  Register #(.width(1)) register_15 (.D(RegWrite_in), .en(ena), .Q(RegWrite_out), .clk(clk), .clr(reset));
  Register #(.width(1)) register_16 (.D(MemRead_in), .en(ena), .Q(MemRead_out), .clk(clk), .clr(reset));
  Register #(.width(1)) register_17 (.D(MemWrite_in), .en(ena), .Q(MemWrite_out), .clk(clk), .clr(reset));
  Register #(.width(1)) register_18 (.D(Branch_in), .en(ena), .Q(Branch_out), .clk(clk), .clr(reset));
  Register #(.width(6)) register_19 (.D(opcode), .en(ena), .Q(opcode_2), .clk(clk), .clr(reset));
  Register #(.width(4)) register_20 (.D(Selec_de_ALU_in), .en(ena), .Q(Selec_de_ALU_out), .clk(clk), .clr(reset));
  Multiplexer multiplexer_1 (.in0(comparator_1_eq), .in1(reset), .out(resx), .sel(ena));  // open: en
  Register #(.width(9)) register_21 (.D(opcoderesult), .en(ena), .Q(opcoderesult_2), .clk(clk), .clr(reset));
  Counter #(.width(2), .max('h1)) counter_1 (
    .D(2'b01), .Q(counter_1_q), .clk(clk), .clr(ena));  // open: load, count, carry
  Comparator #(.width(2)) comparator_1 (.a(2'b01), .b(counter_1_q), .eq(comparator_1_eq));  // open: gt, lt

  // Other names for the same wires on the sheet: res = reset
endmodule

module Mem_Wr (
  input  clk,
  input  reset,
  input  [31:0] RA_in,
  input  [31:0] DO_in,
  input  [4:0] RW_in,
  input  [23:0] pc_in,
  input  [4:0] rs_in,
  input  ENABLEhAZAR,
  input  [4:0] rd_in,
  input  [4:0] rt_in,
  input  MemToReg_in,
  input  RegWrite_in,
  input  MemRead_in,
  input  [5:0] opcode,
  input  ALUsrc_in,
  input  \const ,
  input  [3:0] Selec_de_ALU_in,
  input  [8:0] opcoderesult,
  output [31:0] RA_out,
  output [31:0] DO_out,
  output [4:0] RW_out,
  output [23:0] pc_out,
  output [4:0] rs_out,
  output ENABLE,
  output [4:0] rd_out,
  output [4:0] rt_out,
  output MemToReg_out,
  output RegWrite_out,
  output MemRead_out,
  output [5:0] out_30,
  output ALUsrc_out,
  output cost,
  output [3:0] Selec_de_ALU_out,
  output [8:0] opcoderesult_2
);

  wire and_1_out, comparator_1_eq, comparator_2_eq, not_1_out, undriven, undriven_2, undriven_3;

  Register #(.width(32)) register_1 (.D(RA_in), .Q(RA_out), .clk(clk), .clr(reset));  // open: en
  Register #(.width(32)) register_2 (.D(DO_in), .Q(DO_out), .clk(clk), .clr(reset));  // open: en
  Register #(.width(5)) register_3 (.D(RW_in), .Q(RW_out), .clk(clk), .clr(reset));  // open: en
  Register #(.width(24)) register_4 (.D(pc_in), .Q(pc_out), .clk(clk), .clr(reset));  // open: en
  Register #(.width(5)) register_5 (.D(rs_in), .Q(rs_out), .clk(clk), .clr(reset));  // open: en
  Register #(.width(5)) register_6 (.D(rd_in), .Q(rd_out), .clk(clk), .clr(reset));  // open: en
  Register #(.width(5)) register_7 (.D(rt_in), .Q(rt_out), .clk(clk), .clr(reset));  // open: en
  Register #(.width(1)) register_8 (.D(MemToReg_in), .Q(MemToReg_out), .clk(clk), .clr(reset));  // open: en
  Register #(.width(1)) register_9 (.D(RegWrite_in), .Q(RegWrite_out), .clk(clk), .clr(reset));  // open: en
  Register #(.width(1)) register_10 (.D(MemRead_in), .Q(MemRead_out), .clk(clk), .clr(reset));  // open: en
  Register #(.width(6)) register_11 (.D(opcode), .Q(out_30), .clk(clk), .clr(reset));  // open: en
  Register #(.width(1)) register_12 (.D(ALUsrc_in), .Q(ALUsrc_out), .clk(clk), .clr(reset));  // open: en
  Register #(.width(1)) register_13 (.D(\const ), .en(undriven_3), .Q(cost), .clk(clk), .clr(reset));
  Register #(.width(4)) register_14 (.D(Selec_de_ALU_in), .en(undriven), .Q(Selec_de_ALU_out), .clk(clk), .clr(reset));
  Register #(.width(9)) register_15 (.D(opcoderesult), .en(undriven_2), .Q(opcoderesult_2), .clk(clk), .clr(reset));
  Comparator #(.width(24)) comparator_1 (.a(pc_in), .b({24{1'b0}}), .eq(comparator_1_eq));  // open: gt, lt
  Comparator #(.width(24)) comparator_2 (.a(pc_out), .b(pc_in), .eq(comparator_2_eq));  // open: gt, lt
  not not_1 (not_1_out, comparator_2_eq);
  and and_1 (and_1_out, not_1_out, comparator_1_eq);
  or or_1 (ENABLE, and_1_out, ~ENABLEhAZAR);  // OR_Gate

  // Other names for the same wires on the sheet: res = reset
endmodule

// pc_brach
module Pc_brach (
  input  [23:0] pc_1,
  input  [31:0] offset,
  output [23:0] pc_brach
);

  wire [15:0] bit_extender_1_out;
  wire [23:0] adder_1_out, bit_extender_2_out, subtractor_1_out;

  Bit_Extender #(.in_width(32)) bit_extender_1 (.in(offset), .out(bit_extender_1_out));
  assign bit_extender_2_out = {{9{1'b0}}, bit_extender_1_out[14:0]};  // Bit_Extender bit_extender_2
  Adder #(.width(24)) adder_1 (.a(pc_1), .b(bit_extender_2_out), .out(adder_1_out));  // open: cin, cout
  Subtractor #(.width(24)) subtractor_1 (.a(pc_1), .b(bit_extender_2_out), .out(subtractor_1_out));  // open: bin, bout
  Multiplexer #(.width(24)) multiplexer_1 (
    .in0(adder_1_out), .in1(subtractor_1_out), .out(pc_brach), .sel(bit_extender_1_out[15]));  // open: en
endmodule

module LedInst (
  input  [5:0] Opcode,
  input  ADDI,
  output [31:0] out_3,
  output [31:0] out_4,
  output [31:0] out_5,
  output [31:0] out_6,
  output [31:0] out_7
);

  wire [2:0] Slct;
  wire [5:1] type_inst_1_add;

  type_Inst type_inst_1 (
    .in_1(Opcode), .add(type_inst_1_add[1]), .load(type_inst_1_add[2]), .store(type_inst_1_add[3]),
    .branch(type_inst_1_add[4]), .Jump(type_inst_1_add[5]));  // open: r
  // Probe on Slct
  BitFinder #(.width(7), .\type ("high1")) bitfinder_1 (
    .in({ADDI, type_inst_1_add, 1'b0}), .index(Slct));  // open: found
  Multiplexer #(.select(3), .width(32), .enable("false")) multiplexer_1 (
    .in1(32'h67380000), .in2(32'h8f19c000), .in3(32'h6f98c780), .in4(32'h7798ce90), .in5(32'hfa58b800),
    .in6(32'h67390000), .out(out_3), .sel(Slct));  // open: in0, in7
  Multiplexer #(.select(3), .width(32), .enable("false")) multiplexer_2 (
    .in1(32'h94a40000), .in2(32'h89252000), .in3(32'h82252400), .in4(32'h94a52890), .in5(32'h2255a400),
    .in6(32'h94a50000), .out(out_4), .sel(Slct));  // open: in0, in7
  Multiplexer #(.select(3), .width(32), .enable("false")) multiplexer_3 (
    .in1(32'h94a40000), .in2(32'h89252000), .in3(32'h62254780), .in4(32'hf72528f0), .in5(32'h2252b800),
    .in6(32'h94a50000), .out(out_5), .sel(Slct));  // open: in0, in7
  Multiplexer #(.select(3), .width(32), .enable("false")) multiplexer_4 (
    .in1(32'hf4a40000), .in2(32'h893d2000), .in3(32'h12252400), .in4(32'h953d2890), .in5(32'h2250a000),
    .in6(32'hf4a50000), .out(out_6), .sel(Slct));  // open: in0, in7
  Multiplexer #(.select(3), .width(32), .enable("false")) multiplexer_5 (
    .in1(32'h97bc0000), .in2(32'hef25e000), .in3(32'he2191780), .in4(32'hf4a52e90), .in5(32'he190a000),
    .in6(32'h97bd0000), .out(out_7), .sel(Slct));  // open: in0, in7
endmodule

// Data_Hazard_detec
module Forwarding_unit (
  input  EX_MEM_RegWrite,
  input  [4:0] EX_MEM_Rd,
  input  [4:0] ID_EX_Rt,
  input  [4:0] ID_EX_Rs,
  input  MEM_WB_RegWr,
  input  [4:0] MEM_WB_Rd,
  output hazard,
  output [1:0] ForwardA,
  output [1:0] ForwardB
);

  wire comparator_1_eq, comparator_2_eq, comparator_3_eq, comparator_4_eq, comparator_5_eq, comparator_6_eq,
       comparator_7_eq, comparator_8_eq;

  Comparator #(.width(5)) comparator_1 (.a(EX_MEM_Rd), .b({5{1'b0}}), .eq(comparator_1_eq));  // open: gt, lt
  Comparator #(.width(5)) comparator_2 (.a(EX_MEM_Rd), .b(ID_EX_Rs), .eq(comparator_2_eq));  // open: gt, lt
  Comparator #(.width(5)) comparator_3 (.a(EX_MEM_Rd), .b(ID_EX_Rt), .eq(comparator_3_eq));  // open: gt, lt
  Comparator #(.width(5)) comparator_4 (.a({5{1'b0}}), .b(MEM_WB_Rd), .eq(comparator_4_eq));  // open: gt, lt
  Comparator #(.width(5)) comparator_5 (.a(EX_MEM_Rd), .b(ID_EX_Rs), .eq(comparator_5_eq));  // open: gt, lt
  Comparator #(.width(5)) comparator_6 (.a(MEM_WB_Rd), .b(ID_EX_Rs), .eq(comparator_6_eq));  // open: gt, lt
  Comparator #(.width(5)) comparator_7 (.a(EX_MEM_Rd), .b(ID_EX_Rt), .eq(comparator_7_eq));  // open: gt, lt
  Comparator #(.width(5)) comparator_8 (.a(MEM_WB_Rd), .b(ID_EX_Rt), .eq(comparator_8_eq));  // open: gt, lt
  and and_1 (ForwardA[1], ~comparator_1_eq, EX_MEM_RegWrite, comparator_2_eq);  // AND_Gate
  and and_2 (ForwardB[1], ~comparator_1_eq, comparator_3_eq, EX_MEM_RegWrite);  // AND_Gate
  and and_3 (ForwardA[0], MEM_WB_RegWr, ~comparator_4_eq, ~comparator_5_eq, comparator_6_eq);  // AND_Gate
  and and_4 (ForwardB[0], MEM_WB_RegWr, ~comparator_4_eq, ~comparator_7_eq, comparator_8_eq);  // AND_Gate
  or or_1 (hazard, ForwardA[1], ForwardB[1], ForwardA[0], ForwardB[0]);

  // Notes on the sheet:
  //   1if-> fa=2  10
  //   2if ->fb= 2 10
  //   3if ->fa =1 01
  //   4 if ->fb= 1 01
endmodule

module ALUcontrol (
  input  [1:0] ALUOp,
  input  [5:0] funct,
  output [3:0] out_3
);

  wire and_1_out, and_2_out, and_3_out, and_4_out, and_5_out, and_6_out, not_1_out, not_2_out, not_3_out,
       not_4_out, not_5_out, not_6_out, not_7_out, not_8_out;

  not not_1 (not_1_out, ALUOp[1]);
  not not_2 (not_2_out, funct[2]);
  not not_3 (not_3_out, ALUOp[1]);
  not not_4 (not_4_out, funct[2]);
  not not_5 (not_5_out, funct[3]);
  not not_6 (not_6_out, funct[1]);
  not not_7 (not_7_out, funct[2]);
  not not_8 (not_8_out, funct[0]);
  and and_1 (and_1_out, not_1_out, ALUOp[0]);
  and and_2 (and_2_out, ALUOp[1], not_2_out, funct[0]);
  and and_3 (and_3_out, ALUOp[1], funct[1]);
  and and_4 (and_4_out, ALUOp[1], funct[3]);
  or or_1 (out_3[1], not_3_out, not_4_out, funct[1], funct[3]);
  and and_5 (and_5_out, ALUOp[1], not_5_out, funct[2], not_6_out, funct[0]);
  and and_6 (and_6_out, ALUOp[1], funct[3], not_7_out, funct[1], not_8_out);
  or or_2 (out_3[2], and_1_out, and_2_out, and_3_out, and_4_out);
  or or_3 (out_3[0], and_5_out, and_6_out);

  assign out_3[3] = 1'b0;
endmodule

module ALU (
  input  [31:0] DATA1,
  input  [31:0] DATA2,
  input  [3:0] AluControl,
  output [31:0] RESULT,
  output Zero
);

  wire comparator_1_eq, comparator_2_eq, comparator_3_eq, comparator_4_eq;
  wire [2:0] priority_encoder_1_out;
  wire [31:0] add, \and , \or , Sub;

  Comparator #(.width(4)) comparator_1 (.a(AluControl), .b(4'b0010), .eq(comparator_1_eq));  // open: gt, lt
  Comparator #(.width(4)) comparator_2 (.a(AluControl), .b(4'b0110), .eq(comparator_2_eq));  // open: gt, lt
  Comparator #(.width(4)) comparator_3 (.a(AluControl), .b(4'b0000), .eq(comparator_3_eq));  // open: gt, lt
  Comparator #(.width(4)) comparator_4 (.a(AluControl), .b(4'b0001), .eq(comparator_4_eq));  // open: gt, lt
  Adder #(.width(32)) adder_1 (.a(DATA1), .b(DATA2), .out(add));  // open: cin, cout
  Subtractor #(.width(32)) subtractor_1 (.a(DATA1), .b(DATA2), .out(Sub));  // open: bin, bout
  Comparator #(.width(32)) comparator_5 (.a(DATA1), .b(DATA2), .eq(Zero));  // open: gt, lt
  Priority_Encoder priority_encoder_1 (
    .in0(comparator_1_eq), .in1(comparator_2_eq), .in2(comparator_3_eq), .in3(comparator_4_eq),
    .out(priority_encoder_1_out));  // open: in4, in5, in6, in7, en_in, gs, en_out
  assign \and  = DATA1 & DATA2;  // AND_Gate and_1, 32 bits wide
  assign \or  = DATA1 | DATA2;  // OR_Gate or_1, 32 bits wide
  Multiplexer #(.select(3), .width(32), .enable("false")) multiplexer_1 (
    .in0(add), .in1(Sub), .in2(\and ), .in3(\or ), .out(RESULT), .sel(priority_encoder_1_out));  // open: in4, in5, in6, in7

  // Other names for the same wires on the sheet: A[31:0] = DATA1; B[31:0] = DATA2

  // Notes on the sheet:
  //   Add
  //   0010
  //   Substract
  //   0110
  //   and
  //   0000
  //   or
  //   0001
endmodule

module UnidadControl (
  input  ADDI,
  input  [5:0] OP,
  output RegDst,
  output AluSrc,
  output MentoReg,
  output RegWrite,
  output MenRead,
  output MenWrite,
  output Branch,
  output TipoR,
  output [1:0] ALUOp
);

  wire and_1_out, and_2_out, and_3_out, and_4_out, not_1_out, not_2_out, not_3_out, not_4_out, not_5_out,
       not_6_out, not_7_out, not_8_out, not_9_out, not_10_out, not_11_out, not_12_out, not_13_out,
       not_14_out, not_15_out, not_16_out, not_17_out, not_18_out, not_19_out, not_20_out, not_21_out,
       not_22_out, not_23_out, not_24_out, not_25_out, not_26_out, not_27_out;

  Comparator #(.width(6)) comparator_1 (.a(OP), .b({6{1'b0}}), .eq(TipoR));  // open: gt, lt
  not not_1 (not_1_out, OP[1]);
  not not_2 (not_2_out, OP[2]);
  not not_3 (not_3_out, OP[4]);
  not not_4 (not_4_out, OP[5]);
  not not_5 (not_5_out, OP[5]);
  not not_6 (not_6_out, OP[4]);
  not not_7 (not_7_out, OP[2]);
  not not_8 (not_8_out, OP[1]);
  not not_9 (not_9_out, OP[0]);
  not not_10 (not_10_out, OP[3]);
  not not_11 (not_11_out, OP[1]);
  not not_12 (not_12_out, ADDI);
  and and_1 (and_1_out, not_1_out, not_2_out, OP[3], not_3_out, not_4_out);
  and and_2 (and_2_out, not_5_out, not_6_out, not_7_out, not_8_out, not_9_out);
  not not_13 (not_13_out, OP[3]);
  and and_3 (and_3_out, not_13_out, not_14_out);
  not not_14 (not_14_out, OP[2]);
  and and_4 (and_4_out, not_10_out, OP[1]);
  and and_5 (RegDst, not_11_out, not_12_out);
  or or_1 (AluSrc, OP[1], and_1_out);
  or or_2 (RegWrite, and_2_out, and_3_out);
  not not_15 (not_15_out, ADDI);
  and and_6 (MenWrite, OP[3], not_16_out);
  not not_16 (not_16_out, ADDI);
  not not_17 (not_17_out, OP[5]);
  not not_18 (not_18_out, OP[4]);
  not not_19 (not_19_out, OP[3]);
  not not_20 (not_20_out, OP[2]);
  not not_21 (not_21_out, OP[1]);
  not not_22 (not_22_out, OP[0]);
  not not_23 (not_23_out, OP[5]);
  not not_24 (not_24_out, OP[4]);
  not not_25 (not_25_out, OP[3]);
  not not_26 (not_26_out, OP[1]);
  not not_27 (not_27_out, OP[0]);
  and and_7 (MenRead, and_4_out, not_15_out);
  and and_8 (ALUOp[1], not_17_out, not_18_out, not_19_out, not_20_out, not_21_out, not_22_out);
  and and_9 (ALUOp[0], not_23_out, not_24_out, not_25_out, OP[2], not_26_out, not_27_out);

  assign Branch = OP[2];
  assign MentoReg = OP[1];
endmodule

// Hazard_Control
module Hazard_control (
  input  [23:0] EX_MEM_PC,
  input  [23:0] MEM_WEB_PC,
  input  ENABLEhAZAR,
  output ENABLE
);

  wire and_1_out, comparator_1_eq, comparator_2_eq, not_1_out;

  Comparator #(.width(24)) comparator_1 (.a(EX_MEM_PC), .b({24{1'b0}}), .eq(comparator_1_eq));  // open: gt, lt
  not not_1 (not_1_out, comparator_2_eq);
  Comparator #(.width(24)) comparator_2 (.a(MEM_WEB_PC), .b(EX_MEM_PC), .eq(comparator_2_eq));  // open: gt, lt
  and and_1 (and_1_out, not_1_out, comparator_1_eq);
  or or_1 (ENABLE, and_1_out, ENABLEhAZAR);
endmodule

module matriz_typeInstu (
  input  [5:0] Opcode,
  input  addi,
  input  cnst,
  input  [3:0] alu_SEL,
  input  [8:0] in_5,
  output [31:0] r0,
  output [31:0] m0,
  output [31:0] r1,
  output [31:0] m1,
  output [31:0] r2,
  output [31:0] r3,
  output [31:0] r4
);

  wire comparator_2_eq, comparator_3_eq, Slct2, some;
  wire [2:0] bitfinder_1_index, Slct;
  wire [6:1] comparator_1_eq;
  wire [31:0] multiplexer_2_out, multiplexer_3_out, multiplexer_4_out, multiplexer_5_out, multiplexer_6_out;

  or or_1 (some, comparator_1_eq[3], comparator_1_eq[4], addi, comparator_1_eq[5], comparator_1_eq[6]);
  type_Inst type_inst_1 (
    .in_1(Opcode), .load(comparator_1_eq[3]), .store(comparator_1_eq[4]), .branch(comparator_1_eq[5]),
    .Jump(comparator_1_eq[6]));  // open: r, add
  Comparator #(.width(4)) comparator_1 (.a(alu_SEL), .b(4'b0110), .eq(comparator_1_eq[1]));  // open: gt, lt
  Comparator #(.width(4)) comparator_2 (.a(alu_SEL), .b(4'b0010), .eq(comparator_2_eq));  // open: gt, lt
  Comparator #(.width(9)) comparator_3 (.a(in_5), .b({9{1'b0}}), .eq(comparator_3_eq));  // open: gt, lt
  and and_1 (comparator_1_eq[2], comparator_2_eq, ~some);  // AND_Gate
  // Probe on Slct
  BitFinder #(.width(7), .\type ("high1")) bitfinder_1 (
    .in({comparator_1_eq, addi}), .index(bitfinder_1_index));  // open: found
  Multiplexer #(.width(3)) multiplexer_1 (.in0(3'b111), .in1(bitfinder_1_index), .out(Slct), .sel(Slct2));  // open: en
  and and_2 (Slct2, cnst, ~comparator_3_eq);  // AND_Gate
  DotMatrix #(.inputtype("row"), .matrixcols(32), .matrixrows(5)) dotmatrix_1 (
    .row0(32'h7799c700), .row1(32'h82252800), .row2(32'hf125ce00), .row3(32'h12252800), .row4(32'he1192700));
  DotMatrix #(.inputtype("row"), .matrixcols(32), .matrixrows(5)) dotmatrix_2 (
    .row0(32'h8319c000), .row1(32'h84a52000), .row2(32'h84bd2000), .row3(32'h84a52000), .row4(32'hf325c000));
  DotMatrix #(.inputtype("row"), .matrixcols(32), .matrixrows(5)) dotmatrix_3 (
    .row0(32'h67390000), .row1(32'h94a50000), .row2(32'hf4a50000), .row3(32'h94a50000), .row4(32'h97390000));
  DotMatrix #(.inputtype("row"), .matrixcols(32), .matrixrows(5)) dotmatrix_4 (
    .row0(32'h67382000), .row1(32'h94a49000), .row2(32'hf4a41000), .row3(32'h94a49000), .row4(32'h97382000));
  DotMatrix #(.inputtype("row"), .matrixcols(32), .matrixrows(5)) dotmatrix_5 (
    .row0(32'h9319c008), .row1(32'hd4a52014), .row2(32'hb4a5c022), .row3(32'h94a50014), .row4(32'h93191508));
  DotMatrix #(.inputtype("row"), .matrixcols(32), .matrixrows(5)) dotmatrix_6 (
    .row0(32'h74a5c003), .row1(32'h14bd2041), .row2(32'h14bdc0e0), .row3(32'h94a501f1), .row4(32'h732503fb));
  DotMatrix #(.inputtype("row"), .matrixcols(32), .matrixrows(5)) dotmatrix_7 (
    .row0(32'hce970003), .row1(32'h90948001), .row2(32'hc978700), .row3(32'h82948001), .row4(32'hdc670003));
  Multiplexer #(.width(32)) multiplexer_2 (.in0({32{1'b0}}), .out(multiplexer_2_out), .sel(Slct2));  // open: in1, en
  Multiplexer #(.width(32)) multiplexer_3 (
    .in0({32{1'b0}}), .in1(32'hd4a52014), .out(multiplexer_3_out), .sel(Slct2));  // open: en
  Multiplexer #(.width(32)) multiplexer_4 (
    .in0({32{1'b0}}), .in1(32'hb4a5c022), .out(multiplexer_4_out), .sel(Slct2));  // open: en
  Multiplexer #(.width(32)) multiplexer_5 (
    .in0({32{1'b0}}), .in1(32'h94a50014), .out(multiplexer_5_out), .sel(Slct2));  // open: en
  Multiplexer #(.width(32)) multiplexer_6 (
    .in0({32{1'b0}}), .in1(32'h93191508), .out(multiplexer_6_out), .sel(Slct2));  // open: en
  DotMatrix #(.inputtype("row"), .matrixcols(32), .matrixrows(5)) dotmatrix_8 (
    .row0(32'he7192748), .row1(32'h94a5a848), .row2(32'hf73d6878), .row3(32'h95252848), .row4(32'he4a52748));
  Multiplexer #(.select(3), .width(32)) multiplexer_7 (
    .in0(32'h67390000), .in1(32'hce970003), .in2(32'h67382000), .in3(32'h8319c000), .in4(32'h7799c700),
    .in5(32'he7192748), .in6(32'h74a5c003), .in7(multiplexer_2_out), .out(r0), .sel(Slct));  // open: en
  Multiplexer #(.select(3), .width(32)) multiplexer_8 (
    .in0(32'h94a50000), .in1(32'h90948001), .in2(32'h94a49000), .in3(32'h84a52000), .in4(32'h82252800),
    .in5(32'h94a5a848), .in6(32'h14bd2041), .in7(multiplexer_3_out), .out(r1), .sel(Slct));  // open: en
  Multiplexer #(.select(3), .width(32)) multiplexer_9 (
    .in0(32'hf4a50000), .in1(32'hc978700), .in2(32'hf4a41000), .in3(32'h84bd2000), .in4(32'hf125ce00),
    .in5(32'hf73d6878), .in6(32'h14bdc0e0), .in7(multiplexer_4_out), .out(r2), .sel(Slct));  // open: en
  Multiplexer #(.select(3), .width(32)) multiplexer_10 (
    .in0(32'h94a50000), .in1(32'h82948001), .in2(32'h94a49000), .in3(32'h84a52000), .in4(32'h12252800),
    .in5(32'h95252848), .in6(32'h94a501f1), .in7(multiplexer_5_out), .out(r3), .sel(Slct));  // open: en
  Multiplexer #(.select(3), .width(32)) multiplexer_11 (
    .in0(32'h97390000), .in1(32'hdc670003), .in2(32'h97382000), .in3(32'hf325c000), .in4(32'he1192700),
    .in5(32'he4a52748), .in6(32'h732503fb), .in7(multiplexer_6_out), .out(r4), .sel(Slct));  // open: en
  DotMatrix #(.inputtype("row"), .matrixcols(32), .matrixrows(5)) dotmatrix_9 (
    .row0(r0), .row1(r1), .row2(r2), .row3(r3), .row4(r4));
  DotMatrix #(.inputtype("row"), .matrixcols(32), .matrixrows(2), .dotshape("circle")) dotmatrix_10 (
    .row0(32'haaaaaa55), .row1(m1));
  assign m1 = ~32'haaaaaa55;  // NOT_Gate not_1, 32 bits wide

  assign m0 = 32'haaaaaa55;

  // Other names for the same wires on the sheet: row1[31:0] = r0; row2[31:0] = r1; row3[31:0] = r2; row4[31:0] = r3;
  //   row5[31:0] = r4

  // Notes on the sheet:
  //   b0
  //   b1
  //   b2
  //   b3
  //   b4
endmodule

module PC_display (
  input  \const ,
  input  [23:0] in_2,
  output a,
  output b,
  output c,
  output d,
  output e,
  output f,
  output g
);

  wire and_1_out, and_2_out, and_3_out, and_4_out, and_5_out, and_6_out, and_7_out, and_8_out, and_9_out,
       and_10_out, and_11_out, and_12_out, and_13_out, and_14_out, and_15_out, and_16_out, not_1_out,
       not_2_out, not_3_out, not_4_out, not_5_out, not_6_out, not_7_out, not_8_out, not_9_out, not_10_out,
       not_11_out, not_12_out, not_13_out, not_14_out, not_15_out, not_16_out, not_17_out, not_18_out,
       not_19_out, not_20_out, not_21_out, or_1_out, or_2_out, or_3_out, or_4_out, or_5_out, or_6_out,
       or_7_out;

  not not_1 (not_1_out, in_2[2]);
  not not_2 (not_2_out, in_2[0]);
  not not_3 (not_3_out, in_2[1]);
  not not_4 (not_4_out, in_2[0]);
  not not_5 (not_5_out, in_2[1]);
  not not_6 (not_6_out, in_2[2]);
  not not_7 (not_7_out, in_2[0]);
  not not_8 (not_8_out, in_2[2]);
  not not_9 (not_9_out, in_2[0]);
  not not_10 (not_10_out, in_2[1]);
  not not_11 (not_11_out, in_2[2]);
  not not_12 (not_12_out, in_2[0]);
  not not_13 (not_13_out, in_2[0]);
  not not_14 (not_14_out, in_2[1]);
  not not_15 (not_15_out, in_2[0]);
  not not_16 (not_16_out, in_2[1]);
  not not_17 (not_17_out, in_2[0]);
  not not_18 (not_18_out, in_2[2]);
  not not_19 (not_19_out, in_2[1]);
  not not_20 (not_20_out, in_2[0]);
  and and_1 (and_1_out, not_1_out, not_2_out);
  and and_2 (and_2_out, in_2[2], in_2[0]);
  not not_21 (not_21_out, in_2[2]);
  and and_3 (and_3_out, not_3_out, not_4_out);
  and and_4 (and_4_out, in_2[1], in_2[0]);
  or or_1 (or_1_out, not_5_out, in_2[0], in_2[2]);
  and and_5 (and_5_out, not_6_out, not_7_out);
  and and_6 (and_6_out, not_8_out, in_2[1]);
  and and_7 (and_7_out, in_2[1], not_9_out);
  and and_8 (and_8_out, in_2[2], not_10_out, in_2[0]);
  and and_9 (and_9_out, not_11_out, not_12_out);
  and and_10 (and_10_out, in_2[1], not_13_out);
  and and_11 (and_11_out, not_14_out, not_15_out);
  and and_12 (and_12_out, in_2[2], not_16_out);
  and and_13 (and_13_out, in_2[2], not_17_out);
  and and_14 (and_14_out, not_18_out, in_2[1]);
  and and_15 (and_15_out, in_2[2], not_19_out);
  and and_16 (and_16_out, in_2[2], not_20_out);
  or or_2 (or_2_out, and_1_out, in_2[1], and_2_out, in_2[3]);
  or or_3 (or_3_out, not_21_out, and_3_out, and_4_out);
  or or_4 (or_4_out, and_5_out, and_6_out, and_7_out, and_8_out);
  or or_5 (or_5_out, and_9_out, and_10_out);
  or or_6 (or_6_out, and_11_out, and_12_out, and_13_out, in_2[3]);
  or or_7 (or_7_out, and_14_out, and_15_out, and_16_out, in_2[3]);
  Multiplexer multiplexer_1 (.in0(1'b0), .in1(or_2_out), .out(a), .sel(\const ));  // open: en
  Multiplexer multiplexer_2 (.in0(1'b0), .in1(or_3_out), .out(b), .sel(\const ));  // open: en
  Multiplexer multiplexer_3 (.in0(1'b0), .in1(or_1_out), .out(c), .sel(\const ));  // open: en
  Multiplexer multiplexer_4 (.in0(1'b0), .in1(or_4_out), .out(d), .sel(\const ));  // open: en
  Multiplexer multiplexer_5 (.in0(1'b0), .in1(or_5_out), .out(e), .sel(\const ));  // open: en
  Multiplexer multiplexer_6 (.in0(1'b0), .in1(or_6_out), .out(f), .sel(\const ));  // open: en
  Multiplexer multiplexer_7 (.in0(1'b0), .in1(or_7_out), .out(g), .sel(\const ));  // open: en
  _7_Segment_Display u_7_segment_display_1 (.g(g), .f(f), .a(a), .b(b), .e(e), .d(d), .c(c));  // open: dp

  // Other names for the same wires on the sheet: con = \const 
endmodule

module \const  (
  input  a,
  input  b,
  output c
);

  wire not_1_out, not_2_out;

  not not_1 (not_1_out, a);
  not not_2 (not_2_out, b);
  and and_1 (c, not_1_out, not_2_out);
endmodule

module test (
  input  [23:0] in_1,
  input  [31:0] in_2,
  input  in_3,
  input  in_4,
  input  in_5,
  input  in_6,
  input  in_7,
  input  [31:0] in_8,
  input  [31:0] in_9,
  input  [31:0] in_10,
  input  [31:0] in_11,
  input  [31:0] in_12,
  output [31:0] out_13
);

  RAM #(.addrWidth(24), .dataWidth(32), .bus("separate")) ram_1 (
    .addr(in_1), .din(in_2), .data(out_13), .sel(in_4), .clk(in_5), .ld(in_6), .clr(in_7));  // open: str
  // Probe on in_8
  // Probe on in_9
  // Probe on in_10
  // Probe on in_11
  // Probe on in_12
  DotMatrix #(.inputtype("row"), .matrixcols(32), .matrixrows(5)) dotmatrix_1 (
    .row0(in_8), .row1(in_9), .row2(in_10), .row3(in_11), .row4(in_12));
endmodule

module Hazard_detection_unit (
  input  ID_EX_MemRead,
  input  [4:0] ID_EX_RegisterRt,
  input  [4:0] IF_ID_RegisterRs,
  input  [4:0] IF_ID_RegisterRT,
  output Stall
);

  wire and_1_out, comparator_1_eq, comparator_2_eq, or_1_out;

  Comparator #(.width(5)) comparator_1 (
    .a(ID_EX_RegisterRt), .b(IF_ID_RegisterRs), .eq(comparator_1_eq));  // open: gt, lt
  Comparator #(.width(5)) comparator_2 (
    .a(ID_EX_RegisterRt), .b(IF_ID_RegisterRT), .eq(comparator_2_eq));  // open: gt, lt
  or or_1 (or_1_out, comparator_1_eq, comparator_2_eq);
  and and_1 (and_1_out, ID_EX_MemRead, or_1_out);
  not not_1 (Stall, and_1_out);
endmodule

// 0-9
module Circuito0_9 (
  input  Q3,
  input  Q2,
  input  Q1,
  input  Q0,
  output D3,
  output D2,
  output D1,
  output D0
);

  wire and_1_out, and_2_out, and_3_out, and_4_out, and_5_out, and_6_out, and_7_out, not_1_out, not_2_out,
       not_3_out, not_4_out, not_5_out, not_6_out, not_7_out;

  and and_1 (and_1_out, Q2, Q1, Q0);
  and and_2 (and_2_out, Q3, not_1_out);
  not not_1 (not_1_out, Q0);
  not not_2 (not_2_out, Q2);
  and and_3 (and_3_out, not_2_out, Q1, Q0);
  and and_4 (and_4_out, Q2, not_3_out);
  not not_3 (not_3_out, Q1);
  and and_5 (and_5_out, Q2, not_4_out);
  not not_4 (not_4_out, Q0);
  not not_5 (not_5_out, Q3);
  and and_6 (and_6_out, not_5_out, not_6_out, Q0);
  not not_6 (not_6_out, Q1);
  and and_7 (and_7_out, Q1, not_7_out);
  not not_7 (not_7_out, Q0);
  not not_8 (D0, Q0);
  or or_1 (D3, and_1_out, and_2_out);
  or or_2 (D2, and_3_out, and_4_out, and_5_out);
  or or_3 (D1, and_6_out, and_7_out);
endmodule

module Contador0_9 (
  input  Clock,
  input  Reset,
  input  Reset_1,
  output [3:0] Salida_contador_0_9,
  output [3:0] Salida_estado_actual
);

  wire circuito0_9_1_d0, circuito0_9_1_d1, circuito0_9_1_d2, circuito0_9_1_d3, demultiplexer_1_out0,
       demultiplexer_1_out1;

  D_Flip_Flop d_ff_1 (
    .clk(Clock), .D(circuito0_9_1_d3), .Q(Salida_contador_0_9[3]), .Qn(Salida_estado_actual[3]), .reset(Reset));  // open: preset, en
  D_Flip_Flop d_ff_2 (
    .clk(Clock), .D(circuito0_9_1_d2), .Q(Salida_contador_0_9[2]), .Qn(Salida_estado_actual[2]), .reset(Reset));  // open: preset, en
  D_Flip_Flop d_ff_3 (
    .clk(Clock), .D(circuito0_9_1_d1), .Q(Salida_contador_0_9[1]), .Qn(Salida_estado_actual[1]), .reset(Reset));  // open: preset, en
  Demultiplexer #(.enable("false")) demultiplexer_1 (
    .out0(demultiplexer_1_out0), .out1(demultiplexer_1_out1), .in(Reset), .sel(Reset_1));
  Circuito0_9 circuito0_9_1 (
    .Q3(Salida_contador_0_9[3]), .Q2(Salida_contador_0_9[2]), .Q1(Salida_contador_0_9[1]),
    .Q0(Salida_contador_0_9[0]), .D3(circuito0_9_1_d3), .D2(circuito0_9_1_d2), .D1(circuito0_9_1_d1),
    .D0(circuito0_9_1_d0));
  D_Flip_Flop d_ff_4 (
    .clk(Clock), .D(circuito0_9_1_d0), .Q(Salida_contador_0_9[0]), .Qn(Salida_estado_actual[0]),
    .preset(demultiplexer_1_out1), .reset(demultiplexer_1_out0));  // open: en
  Hex_Digit_Display hex_digit_display_1 (.value(Salida_contador_0_9));  // open: dp
endmodule

module PC_Display (
  input  cant,
  input  clock,
  input  reset,
  output [3:0] Unidad,
  output [3:0] Decena
);

  wire and_1_out, and_2_out, nor_1_out, nor_2_out;
  wire [3:0] contador0_9_1_salida_contador_0_9, contador0_9_1_salida_estado_actual,
       contador0_9_2_salida_contador_0_9, contador0_9_2_salida_estado_actual;

  and and_1 (and_1_out, nor_1_out, and_2_out);
  Hex_Digit_Display hex_digit_display_1 (.value(Decena));  // open: dp
  Multiplexer #(.width(4)) multiplexer_1 (
    .in0(4'b0000), .in1(contador0_9_1_salida_contador_0_9), .out(Decena), .sel(cant));  // open: en
  Contador0_9 contador0_9_1 (
    .Clock(nor_2_out), .Reset(and_1_out), .Reset_1(1'b0),
    .Salida_contador_0_9(contador0_9_1_salida_contador_0_9),
    .Salida_estado_actual(contador0_9_1_salida_estado_actual));
  and and_2 (and_2_out, contador0_9_1_salida_estado_actual[3], ~contador0_9_1_salida_estado_actual[2], ~contador0_9_1_salida_estado_actual[1], contador0_9_1_salida_estado_actual[0]);  // AND_Gate
  Hex_Digit_Display hex_digit_display_2 (.value(Unidad));  // open: dp
  Multiplexer #(.width(4)) multiplexer_2 (
    .in0(4'b0000), .in1(contador0_9_2_salida_contador_0_9), .out(Unidad), .sel(cant));  // open: en
  Contador0_9 contador0_9_2 (
    .Clock(clock), .Reset(and_1_out), .Reset_1(reset),
    .Salida_contador_0_9(contador0_9_2_salida_contador_0_9),
    .Salida_estado_actual(contador0_9_2_salida_estado_actual));
  nor nor_1 (nor_1_out, contador0_9_2_salida_estado_actual[3], contador0_9_2_salida_estado_actual[2], contador0_9_2_salida_estado_actual[1], contador0_9_2_salida_estado_actual[0]);
  nor nor_2 (nor_2_out, contador0_9_2_salida_contador_0_9[3], contador0_9_2_salida_contador_0_9[2], contador0_9_2_salida_contador_0_9[1], contador0_9_2_salida_contador_0_9[0]);

  // Other names for the same wires on the sheet: const = cant
endmodule

module DIS (
  input  CONST,
  input  [23:0] PC,
  output [3:0] DEC,
  output [3:0] UNIT
);

  wire and_1_out, and_2_out, and_3_out, and_4_out, and_5_out, and_6_out, and_7_out, and_8_out, and_9_out,
       and_10_out, not_1_out, not_2_out, not_3_out, not_4_out, not_5_out, not_6_out, not_7_out, not_8_out;
  wire [0:0] or_1_out;
  wire [3:1] or_4_out;

  and and_1 (and_1_out, PC[3], PC[1]);
  and and_2 (and_2_out, PC[3], PC[2]);
  not not_1 (not_1_out, PC[2]);
  not not_2 (not_2_out, PC[1]);
  not not_3 (not_3_out, PC[3]);
  not not_4 (not_4_out, PC[1]);
  not not_5 (not_5_out, PC[4]);
  not not_6 (not_6_out, PC[3]);
  not not_7 (not_7_out, PC[1]);
  not not_8 (not_8_out, PC[1]);
  or or_1 (or_1_out[0], and_1_out, and_2_out, PC[4]);
  and and_3 (and_3_out, PC[3], not_1_out, not_2_out);
  and and_4 (and_4_out, PC[4], PC[1]);
  and and_5 (and_5_out, not_3_out, PC[2]);
  and and_6 (and_6_out, PC[2], PC[1]);
  and and_7 (and_7_out, PC[4], not_4_out);
  and and_8 (and_8_out, not_5_out, not_6_out, PC[1]);
  and and_9 (and_9_out, PC[3], PC[2], not_7_out);
  and and_10 (and_10_out, PC[4], not_8_out);
  or or_2 (or_4_out[3], and_3_out, and_4_out);
  or or_3 (or_4_out[2], and_5_out, and_6_out, and_7_out);
  or or_4 (or_4_out[1], and_8_out, and_9_out, and_10_out);
  Hex_Digit_Display hex_digit_display_1 (.value(DEC));  // open: dp
  Multiplexer #(.width(4)) multiplexer_1 (
    .in0(4'b1110), .in1({3'b000, or_1_out[0]}), .out(DEC), .sel(CONST));  // open: en
  Multiplexer #(.width(4)) multiplexer_2 (.in0(4'b1110), .in1({or_4_out, PC[0]}), .out(UNIT), .sel(CONST));  // open: en
  Hex_Digit_Display hex_digit_display_2 (.value(UNIT));  // open: dp
endmodule
